// Logisim project SAP-1.circ as structural Verilog
module _4_bit_adder_subtractor (
  input  [3:0] a,
  input  [3:0] b,
  input  sub,
  output [3:0] sum,
  output carry_out
);

  wire full_adder_2_carry_out, full_adder_3_carry_out, full_adder_carry_out, xor_1_out, xor_2_out, xor_3_out,
       xor_4_out;

  xor xor_1 (xor_1_out, b[0], sub);
  xor xor_2 (xor_2_out, b[1], sub);
  xor xor_3 (xor_3_out, b[2], sub);
  xor xor_4 (xor_4_out, b[3], sub);
  full_adder full_adder (.a(a[0]), .b(xor_1_out), .c(sub), .sum(sum[0]), .carry_out(full_adder_carry_out));
  full_adder full_adder_2 (
    .a(a[1]), .b(xor_2_out), .c(full_adder_carry_out), .sum(sum[1]), .carry_out(full_adder_2_carry_out));
  full_adder full_adder_3 (
    .a(a[2]), .b(xor_3_out), .c(full_adder_2_carry_out), .sum(sum[2]), .carry_out(full_adder_3_carry_out));
  full_adder full_adder_4 (.a(a[3]), .b(xor_4_out), .c(full_adder_3_carry_out), .sum(sum[3]), .carry_out(carry_out));
endmodule

module full_adder (
  input  a,
  input  b,
  input  c,
  output sum,
  output carry_out
);

  wire and_1_out, and_2_out, xor_1_out, xor_2_out;

  xor xor_1 (xor_1_out, b, c);
  and and_1 (and_1_out, a, b);
  xor xor_2 (xor_2_out, a, b);
  xor xor_3 (sum, a, xor_1_out);
  and and_2 (and_2_out, xor_2_out, c);
  or or_1 (carry_out, and_1_out, and_2_out);
endmodule

module TTL_adder_subtractor (
  input  [7:0] a,
  input  [7:0] b,
  input  sub,
  output [7:0] sum,
  output carry_out
);

  wire _4_bit_adder_subtractor_carry_out, full_adder_2_carry_out, full_adder_3_carry_out,
       full_adder_carry_out, xor_1_out, xor_2_out, xor_3_out, xor_4_out;

  _4_bit_adder_subtractor _4_bit_adder_subtractor (
    .a(a[3:0]), .b(b[3:0]), .sub(sub), .sum(sum[3:0]), .carry_out(_4_bit_adder_subtractor_carry_out));
  xor xor_1 (xor_1_out, b[4], sub);
  xor xor_2 (xor_2_out, b[5], sub);
  xor xor_3 (xor_3_out, b[6], sub);
  xor xor_4 (xor_4_out, b[7], sub);
  full_adder full_adder (
    .a(a[4]), .b(xor_1_out), .c(_4_bit_adder_subtractor_carry_out), .sum(sum[4]),
    .carry_out(full_adder_carry_out));
  full_adder full_adder_2 (
    .a(a[5]), .b(xor_2_out), .c(full_adder_carry_out), .sum(sum[5]), .carry_out(full_adder_2_carry_out));
  full_adder full_adder_3 (
    .a(a[6]), .b(xor_3_out), .c(full_adder_2_carry_out), .sum(sum[6]), .carry_out(full_adder_3_carry_out));
  full_adder full_adder_4 (.a(a[7]), .b(xor_4_out), .c(full_adder_3_carry_out), .sum(sum[7]), .carry_out(carry_out));
endmodule

module D_flip_flop (
  input  d,
  input  preset,
  input  clr,
  output q,
  output q_prime
);

  wire and_1_out, and_2_out, clock_1_out, nand_1_out, nand_2_out, not_1_out;

  Clock clock_1 (.out(clock_1_out));
  not not_1 (not_1_out, d);
  nand nand_1 (nand_1_out, d, clock_1_out);
  nand nand_2 (nand_2_out, not_1_out, clock_1_out);
  and and_1 (and_1_out, nand_1_out, preset);
  and and_2 (and_2_out, nand_2_out, clr);
  nor nor_1 (q, and_1_out, q_prime);
  nor nor_2 (q_prime, q, and_2_out);
endmodule

module edge_triggered_D_flip_flop (
  input  PRESET,
  input  D,
  input  CLEAR,
  output Q,
  output Q_prime
);

  wire clock_1_out, nand_1_out, nand_2_out, nand_3_out, nand_4_out;

  Clock clock_1 (.out(clock_1_out));
  nand nand_1 (nand_1_out, PRESET, nand_4_out, nand_2_out);
  nand nand_2 (nand_2_out, nand_1_out, CLEAR, clock_1_out);
  nand nand_3 (nand_3_out, nand_2_out, clock_1_out, nand_4_out);
  nand nand_4 (nand_4_out, nand_3_out, D, CLEAR);
  nor nor_1 (Q, PRESET, nand_2_out, Q_prime);
  nor nor_2 (Q_prime, Q, nand_3_out, CLEAR);
endmodule
